# Fritzing sketch board (saved by Fritzing 0.9.3b)
circuit board: 5.36223cm x 5.44688cm
breadboards: 2

parts:
  M1 = DC Motor
  M2 = DC Motor
  J1 = Screw terminal - 2 pins [package=THT]
  J2 = Screw terminal - 2 pins [package=THT]
  BT2 = Bluetooth HC-06u [package=THT]
  IC1 = Voltage Regulator [package=78xxl]
  J3 = female pin header, 8 pins [form="♀ (female)"]
  J4 = female pin header, 8 pins [form="♀ (female)"]
  J5 = male pin header, 8 pins [form="♂ (male)"]
  J6 = male pin header, 2 pins [form="♂ (male)"]
  J7 = male pin header, 12 pins [form="♂ (male)"]
  Part1 = Arduino Nano (Rev3.0)
  LED1 = smd LED [color="Red (633nm)" package="0603 [SMD]"]
  R1 = Resistor [tolerance=±5% resistance=220 package="0805 [SMD]"]

nets:
  N1: M1.pin_1, J1.pin1, J4.pin4
  N2: M1.pin_2, J1.pin2, J4.pin3
  N3: M2.pin_1, J2.pin2, J4.pin6
  N4: M2.pin_2, J2.pin1, J4.pin5
  VCC: BT2.VCC, IC1.OUT, Part1.VIN
  GND: BT2.GND, IC1.GND, J3.pin1, J4.pin1, J7.pin12, Part1.GND, R1.Pin_1
  N5: BT2.TXD, Part1.D1/TX
  N6: BT2.RXD, Part1.D0/RX
  N7: IC1.IN, J6.pin2
  N8: J3.pin2, J6.pin1
  N9: J3.pin3, J7.pin11, Part1.D2, LED1.anode
  N10: J3.pin4, J7.pin10, Part1.D3
  N11: J3.pin5, J7.pin9, Part1.D4
  N12: J3.pin6, J7.pin8, Part1.D5
  N13: J3.pin7, J7.pin7, Part1.D6
  N14: J3.pin8, Part1.A0
  N15: J5.pin1, Part1.A1
  N16: J5.pin2, Part1.A2
  N17: J5.pin3, Part1.A3
  N18: J5.pin4, Part1.A4
  N19: J5.pin5, Part1.A5
  N20: J5.pin6, Part1.A6
  N21: J5.pin7, Part1.A7
  N22: J5.pin8, Part1.5V
  N23: J7.pin1, Part1.D12/MISO
  N24: J7.pin2, Part1.D11/MOSI
  N25: J7.pin3, Part1.D10
  N26: J7.pin4, Part1.D9
  N27: J7.pin5, Part1.D8
  N28: J7.pin6, Part1.D7
  N29: LED1.cathode, R1.Pin_0

notes:
  M.D.O
  TRACKer V1.0
  DRV8833
  7805
  Arduino NANO
  Sensores
  Bluetooth
  I/O
  GND
  PowerON
  +  -
  5V

custom parts:
  Bluetooth HC-06u: Bluetooth HC-06 - face up, pins down 16.5mm x 37.5mm PCB
